# Fritzing sketch Esquematico_Tesis (saved by Fritzing 1.0.5)

parts:
  A1 = ESP32 DevKitc V4
  Part1 = InvenSense MPU6050
  M3 = MDD10A
  BAT1 = Lithium Ion Polymer Battery 11.1v 5000mah
  M4 = RioRand LM2596
  CUI-enc1 = AMT103
  M2 = DC Motor [voltage_(max)=6V voltage_(min)=3V]
  M1 = DC Motor [voltage_(max)=6V voltage_(min)=3V]
  CUI-enc2 = AMT103
  microSD1 = MicroSD Card Module
  Fuse2 = Fuse with Handler [part_number=Htc-15m]

nets:
  VCC: A1.Pin_1, Part1.VCC, CUI-enc1.5V
  N1: A1.Pin_7, M3.DIR1
  N2: A1.Pin_8, M3.PWM1
  N3: A1.Pin_10, M3.DIR2
  N4: A1.Pin_11, M3.PWM2
  GND: A1.Pin_14, A1.Pin_38, Part1.GND, M3.Bat-, M3.GND, BAT1.negative, M4.Pin_2, M4.Pin_4, CUI-enc1.GND, microSD1.GND
  N5: A1.Pin_19, M4.Pin_3, microSD1.VCC
  N6: A1.Pin_27, CUI-enc1.A
  N7: A1.Pin_28, CUI-enc1.B
  N8: A1.Pin_29, microSD1.CS
  N9: A1.Pin_30, microSD1.SCK
  N10: A1.Pin_31, microSD1.MISO
  N11: A1.Pin_33, Part1.SDA
  N12: A1.Pin_34, CUI-enc2.A
  N13: A1.Pin_35, CUI-enc2.B
  N14: A1.Pin_36, Part1.SCL
  N15: A1.Pin_37, microSD1.MOSI
  N16: M3.M1B-1, M2.pin_1
  N17: M3.M1A1, M2.pin_2
  N18: M3.Bat+, M4.Pin_1
  N19: M3.M2A-1, M1.pin_2
  N20: M3.M2B-1, M1.pin_1
  N21: BAT1.positive, Fuse2.Connector1

notes:
  Encoders
  IMU
  MicroSD
  ESP32
  Bateria LiPo 11.1V
  Regulador de Voltaje
  Puente H
  Motores DC

custom parts:
  ESP32 DevKitc V4: ESP32-DevKitC board with ESP32-WROOM-32 module. ESP32-DevKitC V4 is a small-sized ESP32-based development board produced by Espressif. Most of the pins on the ESP module are broken out to the pin headers on the board. The pins D0, D1, D2, D3, CMD and CLK are used internally for communication between ESP32 and SPI flash memory. They are grouped on both sides near the USB connector. Avoid using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
